# Fritzing sketch AM2302_MPL115A2 (saved by Fritzing 0.9.0b)
breadboards: 1

parts:
  パーツ1 = Arduino Uno (Rev3)
  RHT1 = Humidity and Temperature Sensor RHT03
  R1(10k) = Resistor [package="2512 [SMD]"]
  U1 = _h3_MPL115A1 (SPI) and MPL115A2 (I2C) Miniature Digital Barometer__h3_ [package=lga8]  # not connected
  C1 = Capacitor [package=cap-pth-small-kit]
  R1 = Resistor [package="2010 [SMD]"]
  R2 = Resistor [package="2010 [SMD]"]

nets:
  N1: パーツ1.A0, RHT1.Data-signal, R1(10k).Pin_1
  N2: パーツ1.A4/SDA, R2.Pin_0
  N3: パーツ1.A5/SCL, R1.Pin_0
  5V: パーツ1.5V, RHT1.Vcc, R1(10k).Pin_0, R1.Pin_1, R2.Pin_1
  N4: パーツ1.GND, RHT1.GND_2, C1.1
